// Logisim project SnakeProject.circ as structural Verilog: 18 circuits, main circuit main
module main (
);

  wire Clock1, Clock2, Clock3, Clock4, Clock5, Clock6, Clock7, clock_1_out, Down, Error, GameLost, GameWon,
       Grow, Left, LeftRightMov, not_1_out, Play, PlayButton, Reset, Right, SoundButton, SoundClock,
       SoundsON, Stop, StopGame, Up, UpDownMov, WallButton, WallMode;
  wire [3:0] SelectedRow;
  wire [6:0] keyboard_in;
  wire [7:0] Food, Score, SnakeHead;
  wire [15:0] displaysystem_1_out0, displaysystem_1_out1, displaysystem_1_out2, displaysystem_1_out3,
       displaysystem_1_out4, displaysystem_1_out5, displaysystem_1_out6, displaysystem_1_out7,
       displaysystem_1_out8, displaysystem_1_out9, displaysystem_1_out10, displaysystem_1_out11,
       displaysystem_1_out12, displaysystem_1_out13, displaysystem_1_out14, displaysystem_1_out15, SnakeBody,
       UpdatedRow;

  Clock #(.highDuration(3), .lowDuration(3)) clock_1 (.out(clock_1_out));
  SoundSystem soundsystem_1 (
    .Reset(Reset), .SoundClock(SoundClock), .SoundsON(SoundsON), .Grow(Grow), .GameWon(GameWon),
    .GameLost(GameLost));
  LED led_1 (.in(GameLost));
  LED led_2 (.in(GameLost));
  LED led_3 (.in(GameLost));
  LED led_4 (.in(GameLost));
  LED led_5 (.in(GameLost));
  LED led_6 (.in(GameLost));
  LED led_7 (.in(GameLost));
  LED led_8 (.in(GameLost));
  LED led_9 (.in(GameLost));
  LED led_10 (.in(GameLost));
  ClockGenerator clockgenerator_1 (
    .Reset(Reset), .MainClock(clock_1_out), .Play(Play), .Clock7(Clock7), .Clock6(Clock6), .Clock5(Clock5),
    .Clock4(Clock4), .Clock3(Clock3), .Clock2(Clock2), .Clock1(Clock1), .SoundClock(SoundClock));
  LED led_11 (.in(GameWon));
  LED led_12 (.in(GameWon));
  LED led_13 (.in(GameWon));
  LED led_14 (.in(GameWon));
  LED led_15 (.in(GameWon));
  LED led_16 (.in(GameWon));
  LED led_17 (.in(GameWon));
  LED led_18 (.in(GameWon));
  FoodGenerator foodgenerator_1 (.Reset(Reset), .Grow(Grow), .Error(Error), .Food(Food));
  LED led_19 (.in(GameWon));
  LED led_20 (.in(GameWon));
  LED led_21 (.in(GameWon));
  LED led_22 (.in(GameWon));
  LED led_23 (.in(GameWon));
  DisplaySystem displaysystem_1 (
    .Reset(Reset), .Clock5(Clock5), .Clock6(Clock6), .UpdatedRow(UpdatedRow), .SelectedRow(SelectedRow),
    .Out0(displaysystem_1_out0), .Out1(displaysystem_1_out1), .Out2(displaysystem_1_out2),
    .Out3(displaysystem_1_out3), .Out4(displaysystem_1_out4), .Out5(displaysystem_1_out5),
    .Out6(displaysystem_1_out6), .Out7(displaysystem_1_out7), .Out8(displaysystem_1_out8),
    .Out9(displaysystem_1_out9), .Out10(displaysystem_1_out10), .Out11(displaysystem_1_out11),
    .Out12(displaysystem_1_out12), .Out13(displaysystem_1_out13), .Out14(displaysystem_1_out14),
    .Out15(displaysystem_1_out15));
  LED led_24 (.in(GameWon));
  LED led_25 (.in(GameWon));
  LED led_26 (.in(GameWon));
  LED led_27 (.in(GameWon));
  LED led_28 (.in(GameWon));
  LED led_29 (.in(GameWon));
  LED led_30 (.in(GameWon));
  LED led_31 (.in(GameWon));
  LED led_32 (.in(GameWon));
  LED led_33 (.in(GameWon));
  LED led_34 (.in(GameWon));
  LED led_35 (.in(GameWon));
  LED led_36 (.in(GameWon));
  Hex_Digit_Display hex_digit_display_1 (.value(Score[7:4]));  // open: dp
  DotMatrix #(.dotshape("circle"), .inputtype("row"), .matrixcols(16), .matrixrows(16)) dotmatrix_1 (
    .row0(displaysystem_1_out0), .row1(displaysystem_1_out1), .row2(displaysystem_1_out2),
    .row3(displaysystem_1_out3), .row4(displaysystem_1_out4), .row5(displaysystem_1_out5),
    .row6(displaysystem_1_out6), .row7(displaysystem_1_out7), .row8(displaysystem_1_out8),
    .row9(displaysystem_1_out9), .row10(displaysystem_1_out10), .row11(displaysystem_1_out11),
    .row12(displaysystem_1_out12), .row13(displaysystem_1_out13), .row14(displaysystem_1_out14),
    .row15(displaysystem_1_out15));
  Keyboard keyboard_1 (.clk(Clock7), .clr(Reset), .data(keyboard_in));  // open: re, avail
  Hex_Digit_Display hex_digit_display_2 (.value(Score[3:0]));  // open: dp
  Comparator comparator_1 (.a(8'h1), .b(Score), .eq(GameWon));  // open: gt, lt
  Button button_1 (.out(Up));
  Button button_2 (.out(Left));
  Button button_3 (.out(Down));
  ManageSystem managesystem_1 (
    .Stop(Stop), .PlayButton(PlayButton), .SoundButton(SoundButton), .WallButton(WallButton), .Reset(Reset),
    .Play(Play), .SoundsON(SoundsON), .WallMode(WallMode));
  Button button_4 (.out(Right));
  RAMSystem ramsystem_1 (
    .Reset(Reset), .Clock1(Clock1), .Clock2(Clock2), .Clock3(Clock3), .Grow(Grow), .SnakeHead(SnakeHead),
    .Score(Score), .SelectedRow(SelectedRow), .SnakeBody(SnakeBody));
  StopSystem stopsystem_1 (
    .Reset(Reset), .StopGame(StopGame), .GameWon(GameWon), .GameLost(GameLost), .Play(Play), .Stop(Stop));
  LED led_37 (.in(Stop));
  Button button_5 (.out(StopGame));
  LED led_38 (.in(Play));
  Button button_6 (.out(PlayButton));
  LED led_39 (.in(WallMode));
  LED led_40 (.in(not_1_out));
  Button button_7 (.out(WallButton));
  LED led_41 (.in(SoundsON));
  Button button_8 (.out(SoundButton));
  not not_1 (not_1_out, WallMode);
  SnakeMovement snakemovement_1 (
    .Reset(Reset), .Up(Up), .Down(Down), .Clock4(Clock4), .Keyboard_in(keyboard_in), .Clock7(Clock7),
    .Left(Left), .Right(Right), .Head_location(SnakeHead), .UpDownMov(UpDownMov), .LeftRightMov(LeftRightMov));
  GameLogic gamelogic_1 (
    .Food(Food), .SnakeHead(SnakeHead), .SnakeBody(SnakeBody), .SelectedRow(SelectedRow),
    .WallMode(WallMode), .Clock5(Clock5), .UpDownMov(UpDownMov), .LeftRightMov(LeftRightMov), .Play(Play),
    .GameLost(GameLost), .Error(Error), .Grow(Grow), .UpdatedRow(UpdatedRow));

  // Notes on the sheet:
  //   C0l15
  //   Press w ,a ,s ,d to move
  //   Reach 5 Score to win :)
  //   Col0
  //   Row0
  //   Row15
  //   STOP Button
  //   PLAY / Restart Button
  //   ON - HardMode
  //   OFF- EasyMode
  //   Wall Mode
  //   Sounds ON
  //   Snake Game
  //   Press Play to Start
endmodule

module REG16x16 (
  input  [15:0] Row_REG,
  input  Clock,
  input  Reset,
  output [15:0] out_4
);

  D_Flip_Flop d_ff_1 (.D(Row_REG[0]), .clk(Clock), .Q(out_4[0]), .reset(Reset));  // open: Qn, preset
  D_Flip_Flop d_ff_2 (.D(Row_REG[2]), .clk(Clock), .Q(out_4[2]), .reset(Reset));  // open: Qn, preset
  D_Flip_Flop d_ff_3 (.D(Row_REG[4]), .clk(Clock), .Q(out_4[4]), .reset(Reset));  // open: Qn, preset
  D_Flip_Flop d_ff_4 (.D(Row_REG[6]), .clk(Clock), .Q(out_4[6]), .reset(Reset));  // open: Qn, preset
  D_Flip_Flop d_ff_5 (.D(Row_REG[8]), .clk(Clock), .Q(out_4[8]), .reset(Reset));  // open: Qn, preset
  D_Flip_Flop d_ff_6 (.D(Row_REG[10]), .clk(Clock), .Q(out_4[10]), .reset(Reset));  // open: Qn, preset
  D_Flip_Flop d_ff_7 (.D(Row_REG[12]), .clk(Clock), .Q(out_4[12]), .reset(Reset));  // open: Qn, preset
  D_Flip_Flop d_ff_8 (.D(Row_REG[14]), .clk(Clock), .Q(out_4[14]), .reset(Reset));  // open: Qn, preset
  D_Flip_Flop d_ff_9 (.D(Row_REG[1]), .clk(Clock), .Q(out_4[1]), .reset(Reset));  // open: Qn, preset
  D_Flip_Flop d_ff_10 (.D(Row_REG[3]), .clk(Clock), .Q(out_4[3]), .reset(Reset));  // open: Qn, preset
  D_Flip_Flop d_ff_11 (.D(Row_REG[5]), .clk(Clock), .Q(out_4[5]), .reset(Reset));  // open: Qn, preset
  D_Flip_Flop d_ff_12 (.D(Row_REG[7]), .clk(Clock), .Q(out_4[7]), .reset(Reset));  // open: Qn, preset
  D_Flip_Flop d_ff_13 (.D(Row_REG[9]), .clk(Clock), .Q(out_4[9]), .reset(Reset));  // open: Qn, preset
  D_Flip_Flop d_ff_14 (.D(Row_REG[11]), .clk(Clock), .Q(out_4[11]), .reset(Reset));  // open: Qn, preset
  D_Flip_Flop d_ff_15 (.D(Row_REG[13]), .clk(Clock), .Q(out_4[13]), .reset(Reset));  // open: Qn, preset
  D_Flip_Flop d_ff_16 (.D(Row_REG[15]), .clk(Clock), .Q(out_4[15]), .reset(Reset));  // open: Qn, preset
endmodule

module RowUpdate (
  input  [15:0] In0,
  input  [15:0] In1,
  input  [15:0] In2,
  input  [15:0] In3,
  input  [15:0] In4,
  input  [15:0] In5,
  input  [15:0] In6,
  input  [15:0] In7,
  input  [15:0] In8,
  input  [15:0] In9,
  input  [15:0] In10,
  input  [15:0] In11,
  input  [15:0] In12,
  input  [15:0] In13,
  input  [15:0] In14,
  input  [15:0] In15,
  input  Reset,
  input  Clock5,
  input  [3:0] SelectedRow,
  output [15:0] Out0,
  output [15:0] Out1,
  output [15:0] Out2,
  output [15:0] Out3,
  output [15:0] Out4,
  output [15:0] Out5,
  output [15:0] Out6,
  output [15:0] Out7,
  output [15:0] Out8,
  output [15:0] Out9,
  output [15:0] Out10,
  output [15:0] Out11,
  output [15:0] Out12,
  output [15:0] Out13,
  output [15:0] Out14,
  output [15:0] Out15
);

  wire demultiplexer_1_out0, demultiplexer_1_out1, demultiplexer_1_out2, demultiplexer_1_out3,
       demultiplexer_1_out4, demultiplexer_1_out5, demultiplexer_1_out6, demultiplexer_1_out7,
       demultiplexer_1_out8, demultiplexer_1_out9, demultiplexer_1_out10, demultiplexer_1_out11,
       demultiplexer_1_out12, demultiplexer_1_out13, demultiplexer_1_out14, demultiplexer_1_out15;

  Demultiplexer #(.select(4)) demultiplexer_1 (
    .out0(demultiplexer_1_out0), .out1(demultiplexer_1_out1), .out2(demultiplexer_1_out2),
    .out3(demultiplexer_1_out3), .out4(demultiplexer_1_out4), .out5(demultiplexer_1_out5),
    .out6(demultiplexer_1_out6), .out7(demultiplexer_1_out7), .out8(demultiplexer_1_out8),
    .out9(demultiplexer_1_out9), .out10(demultiplexer_1_out10), .out11(demultiplexer_1_out11),
    .out12(demultiplexer_1_out12), .out13(demultiplexer_1_out13), .out14(demultiplexer_1_out14),
    .out15(demultiplexer_1_out15), .in(Clock5), .sel(SelectedRow));
  REG16x16 reg16x16_1 (.Row_REG(In0), .Clock(demultiplexer_1_out0), .Reset(Reset), .out_4(Out0));
  REG16x16 reg16x16_2 (.Row_REG(In2), .Clock(demultiplexer_1_out2), .Reset(Reset), .out_4(Out2));
  REG16x16 reg16x16_3 (.Row_REG(In4), .Clock(demultiplexer_1_out4), .Reset(Reset), .out_4(Out4));
  REG16x16 reg16x16_4 (.Row_REG(In6), .Clock(demultiplexer_1_out6), .Reset(Reset), .out_4(Out6));
  REG16x16 reg16x16_5 (.Row_REG(In8), .Clock(demultiplexer_1_out8), .Reset(Reset), .out_4(Out8));
  REG16x16 reg16x16_6 (.Row_REG(In10), .Clock(demultiplexer_1_out10), .Reset(Reset), .out_4(Out10));
  REG16x16 reg16x16_7 (.Row_REG(In12), .Clock(demultiplexer_1_out12), .Reset(Reset), .out_4(Out12));
  REG16x16 reg16x16_8 (.Row_REG(In14), .Clock(demultiplexer_1_out14), .Reset(Reset), .out_4(Out14));
  REG16x16 reg16x16_9 (.Row_REG(In1), .Clock(demultiplexer_1_out1), .Reset(Reset), .out_4(Out1));
  REG16x16 reg16x16_10 (.Row_REG(In3), .Clock(demultiplexer_1_out3), .Reset(Reset), .out_4(Out3));
  REG16x16 reg16x16_11 (.Row_REG(In5), .Clock(demultiplexer_1_out5), .Reset(Reset), .out_4(Out5));
  REG16x16 reg16x16_12 (.Row_REG(In7), .Clock(demultiplexer_1_out7), .Reset(Reset), .out_4(Out7));
  REG16x16 reg16x16_13 (.Row_REG(In9), .Clock(demultiplexer_1_out9), .Reset(Reset), .out_4(Out9));
  REG16x16 reg16x16_14 (.Row_REG(In11), .Clock(demultiplexer_1_out11), .Reset(Reset), .out_4(Out11));
  REG16x16 reg16x16_15 (.Row_REG(In13), .Clock(demultiplexer_1_out13), .Reset(Reset), .out_4(Out13));
  REG16x16 reg16x16_16 (.Row_REG(In15), .Clock(demultiplexer_1_out15), .Reset(Reset), .out_4(Out15));

  // Notes on the sheet:
  //   Input
  //   Output
endmodule

module RowFinal (
  input  [15:0] In0,
  input  [15:0] In1,
  input  [15:0] In2,
  input  [15:0] In3,
  input  [15:0] In4,
  input  [15:0] In5,
  input  [15:0] In6,
  input  [15:0] In7,
  input  [15:0] In8,
  input  [15:0] In9,
  input  [15:0] In10,
  input  [15:0] In11,
  input  [15:0] In12,
  input  [15:0] In13,
  input  [15:0] In14,
  input  [15:0] In15,
  input  Reset,
  input  Clock6,
  output [15:0] Out0,
  output [15:0] Out1,
  output [15:0] Out2,
  output [15:0] Out3,
  output [15:0] Out4,
  output [15:0] Out5,
  output [15:0] Out6,
  output [15:0] Out7,
  output [15:0] Out8,
  output [15:0] Out9,
  output [15:0] Out10,
  output [15:0] Out11,
  output [15:0] Out12,
  output [15:0] Out13,
  output [15:0] Out14,
  output [15:0] Out15
);

  REG16x16 reg16x16_1 (.Row_REG(In0), .Clock(Clock6), .Reset(Reset), .out_4(Out0));
  REG16x16 reg16x16_2 (.Row_REG(In2), .Clock(Clock6), .Reset(Reset), .out_4(Out2));
  REG16x16 reg16x16_3 (.Row_REG(In4), .Clock(Clock6), .Reset(Reset), .out_4(Out4));
  REG16x16 reg16x16_4 (.Row_REG(In6), .Clock(Clock6), .Reset(Reset), .out_4(Out6));
  REG16x16 reg16x16_5 (.Row_REG(In8), .Clock(Clock6), .Reset(Reset), .out_4(Out8));
  REG16x16 reg16x16_6 (.Row_REG(In10), .Clock(Clock6), .Reset(Reset), .out_4(Out10));
  REG16x16 reg16x16_7 (.Row_REG(In12), .Clock(Clock6), .Reset(Reset), .out_4(Out12));
  REG16x16 reg16x16_8 (.Row_REG(In14), .Clock(Clock6), .Reset(Reset), .out_4(Out14));
  REG16x16 reg16x16_9 (.Row_REG(In1), .Clock(Clock6), .Reset(Reset), .out_4(Out1));
  REG16x16 reg16x16_10 (.Row_REG(In3), .Clock(Clock6), .Reset(Reset), .out_4(Out3));
  REG16x16 reg16x16_11 (.Row_REG(In5), .Clock(Clock6), .Reset(Reset), .out_4(Out5));
  REG16x16 reg16x16_12 (.Row_REG(In7), .Clock(Clock6), .Reset(Reset), .out_4(Out7));
  REG16x16 reg16x16_13 (.Row_REG(In9), .Clock(Clock6), .Reset(Reset), .out_4(Out9));
  REG16x16 reg16x16_14 (.Row_REG(In11), .Clock(Clock6), .Reset(Reset), .out_4(Out11));
  REG16x16 reg16x16_15 (.Row_REG(In13), .Clock(Clock6), .Reset(Reset), .out_4(Out13));
  REG16x16 reg16x16_16 (.Row_REG(In15), .Clock(Clock6), .Reset(Reset), .out_4(Out15));

  // Notes on the sheet:
  //   Input
  //   Output
endmodule

module GameLogic (
  input  [7:0] Food,
  input  [7:0] SnakeHead,
  input  [15:0] SnakeBody,
  input  [3:0] SelectedRow,
  input  WallMode,
  input  Clock5,
  input  UpDownMov,
  input  LeftRightMov,
  input  Play,
  output GameLost,
  output Error,
  output Grow,
  output [15:0] UpdatedRow
);

  wire and_2_out, and_3_out, and_4_out, and_5_out, and_6_out, and_7_out, and_10_out, and_11_out,
       comparator_1_eq, comparator_2_eq, comparator_3_eq, comparator_4_eq, comparator_5_eq, comparator_6_eq,
       comparator_6_gt, comparator_7_eq, comparator_8_eq, comparator_9_eq, comparator_10_eq,
       comparator_11_eq, comparator_12_eq, comparator_13_gt, d_ff_1_q, not_1_out, not_2_out, or_1_out,
       or_4_out;
  wire [15:0] and_1_out, and_8_out, decoder_1_out0, decoder_2_out0, FoodFiltered, SnakeHeadFiltered;

  Comparator #(.width(4)) comparator_1 (.a(4'b0000), .b(SnakeHead[3:0]), .eq(comparator_1_eq));  // open: gt, lt
  Comparator #(.width(4)) comparator_2 (.a(4'b1111), .b(SnakeHead[3:0]), .eq(comparator_2_eq));  // open: gt, lt
  Comparator #(.width(4)) comparator_3 (.a(SnakeHead[7:4]), .b(4'b1111), .eq(comparator_3_eq));  // open: gt, lt
  Comparator #(.width(4)) comparator_4 (.a(SnakeHead[7:4]), .b(4'b0000), .eq(comparator_4_eq));  // open: gt, lt
  assign and_1_out = SnakeHeadFiltered & SnakeBody;  // AND_Gate and_1, 16 bits wide
  Decoder #(.select(4)) decoder_1 (
    .out0(decoder_1_out0[0]), .out1(decoder_1_out0[1]), .out2(decoder_1_out0[2]), .out3(decoder_1_out0[3]),
    .out4(decoder_1_out0[4]), .out5(decoder_1_out0[5]), .out6(decoder_1_out0[6]), .out7(decoder_1_out0[7]),
    .out8(decoder_1_out0[8]), .out9(decoder_1_out0[9]), .out10(decoder_1_out0[10]),
    .out11(decoder_1_out0[11]), .out12(decoder_1_out0[12]), .out13(decoder_1_out0[13]),
    .out14(decoder_1_out0[14]), .out15(decoder_1_out0[15]), .sel(Food[3:0]));  // open: en
  Comparator #(.width(4)) comparator_5 (.a(Food[7:4]), .b(SelectedRow), .eq(comparator_5_eq));  // open: gt, lt
  Comparator #(.width(16)) comparator_6 (
    .a(and_1_out), .b({16{1'b0}}), .gt(comparator_6_gt), .eq(comparator_6_eq));  // open: lt
  Multiplexer #(.enable("true"), .width(16)) multiplexer_1 (
    .in0({16{1'b0}}), .in1(decoder_1_out0), .out(FoodFiltered), .sel(comparator_5_eq));  // open: en
  and and_2 (and_2_out, comparator_6_gt, Clock5);
  and and_3 (and_3_out, comparator_1_eq, LeftRightMov);
  not not_1 (not_1_out, LeftRightMov);
  and and_4 (and_4_out, not_1_out, comparator_2_eq);
  and and_5 (and_5_out, comparator_3_eq, not_2_out);
  not not_2 (not_2_out, UpDownMov);
  and and_6 (and_6_out, UpDownMov, comparator_4_eq);
  D_Flip_Flop d_ff_1 (.D(and_2_out), .clk(and_2_out), .Q(d_ff_1_q), .reset(comparator_6_eq));  // open: Qn, preset
  or or_1 (or_1_out, and_3_out, and_4_out, and_5_out, and_6_out);
  and and_7 (and_7_out, or_1_out, WallMode);
  or or_2 (GameLost, d_ff_1_q, and_7_out);
  assign UpdatedRow = FoodFiltered | SnakeHeadFiltered | SnakeBody;  // OR_Gate or_3, 16 bits wide
  Comparator #(.width(4)) comparator_7 (.a(4'b0000), .b(Food[3:0]), .eq(comparator_7_eq));  // open: gt, lt
  Comparator #(.width(4)) comparator_8 (.a(Food[7:4]), .b(4'b0000), .eq(comparator_8_eq));  // open: gt, lt
  Decoder #(.select(4)) decoder_2 (
    .out0(decoder_2_out0[0]), .out1(decoder_2_out0[1]), .out2(decoder_2_out0[2]), .out3(decoder_2_out0[3]),
    .out4(decoder_2_out0[4]), .out5(decoder_2_out0[5]), .out6(decoder_2_out0[6]), .out7(decoder_2_out0[7]),
    .out8(decoder_2_out0[8]), .out9(decoder_2_out0[9]), .out10(decoder_2_out0[10]),
    .out11(decoder_2_out0[11]), .out12(decoder_2_out0[12]), .out13(decoder_2_out0[13]),
    .out14(decoder_2_out0[14]), .out15(decoder_2_out0[15]), .sel(SnakeHead[3:0]));  // open: en
  Comparator #(.width(4)) comparator_9 (.a(SnakeHead[7:4]), .b(SelectedRow), .eq(comparator_9_eq));  // open: gt, lt
  assign and_8_out = SnakeBody & FoodFiltered;  // AND_Gate and_8, 16 bits wide
  Comparator #(.width(4)) comparator_10 (.a(Food[3:0]), .b(4'b1111), .eq(comparator_10_eq));  // open: gt, lt
  Comparator #(.width(4)) comparator_11 (.a(Food[7:4]), .b(4'b1111), .eq(comparator_11_eq));  // open: gt, lt
  Comparator comparator_12 (.a(Food), .b(SnakeHead), .eq(comparator_12_eq));  // open: gt, lt
  and and_9 (Grow, comparator_12_eq, Play);
  Comparator #(.width(16)) comparator_13 (.a(and_8_out), .b({16{1'b0}}), .gt(comparator_13_gt));  // open: eq, lt
  Multiplexer #(.enable("true"), .width(16)) multiplexer_2 (
    .in0({16{1'b0}}), .in1(decoder_2_out0), .out(SnakeHeadFiltered), .sel(comparator_9_eq));  // open: en
  and and_10 (and_10_out, comparator_13_gt, Clock5);
  or or_4 (or_4_out, comparator_7_eq, comparator_10_eq, comparator_11_eq, comparator_8_eq);
  and and_11 (and_11_out, or_4_out, Clock5, WallMode);
  or or_5 (Error, and_10_out, and_11_out);

  // Notes on the sheet:
  //   Left Wall
  //   Up Wall
  //   Right Wall
  //   Down Wall
  //   Food (row,col)
  //   Snake head (row,col)
  //   Snake body vector
  //   Current Row that being read
  //   Display
  //   If snake head equals to the food location the snake grow
  //   Check if the food location is on the snake body or on the wall
endmodule

module SnakeDirection (
  input  Reset,
  input  Up_in,
  input  Down_in,
  input  Left_in,
  input  Right_in,
  input  Clock7,
  output Up_Out,
  output Down_Out,
  output Left_Out,
  output Right_Out
);

  wire and_1_out, and_2_out, and_3_out, and_4_out, d_ff_1_qn, d_ff_2_qn, d_ff_3_qn, d_ff_4_qn, or_1_out,
       or_2_out, or_3_out, or_4_out, or_5_out, or_6_out;

  and and_1 (and_1_out, d_ff_2_qn, Up_in);
  and and_2 (and_2_out, d_ff_1_qn, Down_in);
  and and_3 (and_3_out, d_ff_4_qn, Left_in);
  and and_4 (and_4_out, d_ff_3_qn, Right_in);
  or or_1 (or_1_out, Up_Out, and_1_out);
  or or_2 (or_2_out, Down_Out, and_2_out);
  or or_3 (or_3_out, Left_Out, and_3_out);
  or or_4 (or_4_out, Right_Out, and_4_out);
  D_Flip_Flop d_ff_1 (.D(or_1_out), .clk(Clock7), .Q(Up_Out), .Qn(d_ff_1_qn), .preset(or_1_out), .reset(or_5_out));
  D_Flip_Flop d_ff_2 (.D(or_2_out), .clk(Clock7), .Q(Down_Out), .Qn(d_ff_2_qn), .preset(or_2_out), .reset(or_5_out));
  D_Flip_Flop d_ff_3 (.D(or_3_out), .clk(Clock7), .Q(Left_Out), .Qn(d_ff_3_qn), .preset(or_3_out), .reset(or_6_out));
  D_Flip_Flop d_ff_4 (.D(or_4_out), .clk(Clock7), .Q(Right_Out), .Qn(d_ff_4_qn), .preset(or_4_out), .reset(or_6_out));
  or or_5 (or_5_out, Reset, and_4_out, and_3_out);
  or or_6 (or_6_out, Reset, and_1_out, and_2_out);
endmodule

module SnakeMovement (
  input  Reset,
  input  Up,
  input  Down,
  input  Clock4,
  input  [6:0] Keyboard_in,
  input  Clock7,
  input  Left,
  input  Right,
  output [7:0] Head_location,
  output UpDownMov,
  output LeftRightMov
);

  wire comparator_1_eq, comparator_2_eq, comparator_3_eq, comparator_4_eq, comparator_4_gt, or_1_out,
       or_2_out, or_3_out, or_4_out;

  Comparator #(.width(7)) comparator_1 (.a(Keyboard_in), .b(7'b1110111), .eq(comparator_1_eq));  // open: gt, lt
  Comparator #(.width(7)) comparator_2 (.a(Keyboard_in), .b(7'b1110011), .eq(comparator_2_eq));  // open: gt, lt
  Comparator #(.width(7)) comparator_3 (.a(Keyboard_in), .b(7'b1100001), .eq(comparator_3_eq));  // open: gt, lt
  Comparator #(.width(7)) comparator_4 (
    .a(7'b1100100), .b(Keyboard_in), .gt(comparator_4_gt), .eq(comparator_4_eq));  // open: lt
  or or_1 (or_1_out, comparator_2_eq, Down);
  or or_2 (or_2_out, comparator_3_eq, Left);
  or or_3 (or_3_out, comparator_1_eq, Up);
  or or_4 (or_4_out, comparator_4_eq, Right);
  HeadControler headcontroler_1 (
    .Reset(Reset), .FPS(Clock4), .Up(or_3_out), .Down(or_1_out), .Left(or_2_out), .Right(or_4_out),
    .Clock7(Clock7), .Head_location(Head_location), .UpDownMov(UpDownMov), .LeftRightMov(LeftRightMov));

  // Notes on the sheet:
  //   Hexa because we got an ASCII value
  //   w_keyBtn
  //   s_keyBtn
  //   a_keyBtn
  //   d_keyBtn
endmodule

module HeadControler (
  input  Reset,
  input  FPS,
  input  Up,
  input  Down,
  input  Left,
  input  Right,
  input  Clock7,
  output [7:0] Head_location,
  output UpDownMov,
  output LeftRightMov
);

  wire and_2_out, decoder_1_out0, decoder_1_out1, decoder_1_out2, decoder_2_out0, decoder_2_out1,
       decoder_2_out2, not_1_out, not_2_out, not_3_out, not_4_out, or_1_out;
  wire [1:0] snakedirection_1_left_out, snakedirection_1_up_out;
  wire [3:0] Col_mov, Row_mov;

  SnakeDirection snakedirection_1 (
    .Reset(Reset), .Up_in(Up), .Down_in(Down), .Left_in(Left), .Right_in(Right), .Clock7(Clock7),
    .Up_Out(snakedirection_1_up_out[0]), .Down_Out(snakedirection_1_up_out[1]),
    .Left_Out(snakedirection_1_left_out[0]), .Right_Out(snakedirection_1_left_out[1]));
  Adder #(.width(4)) adder_1 (.a(Row_mov), .b(4'b1110), .out(Head_location[3:0]));  // open: cin, cout
  Adder #(.width(4)) adder_2 (.a(Col_mov), .b(4'b0010), .out(Head_location[7:4]));  // open: cin, cout
  Decoder #(.select(2)) decoder_1 (
    .out0(decoder_1_out0), .out1(decoder_1_out1), .out2(decoder_1_out2), .sel(snakedirection_1_up_out));  // open: out3, en
  not not_1 (not_1_out, decoder_2_out0);
  Decoder #(.select(2)) decoder_2 (
    .out0(decoder_2_out0), .out1(decoder_2_out1), .out2(decoder_2_out2), .sel(snakedirection_1_left_out));  // open: out3, en
  not not_2 (not_2_out, decoder_2_out2);
  not not_3 (not_3_out, decoder_1_out0);
  not not_4 (not_4_out, decoder_1_out1);
  or or_1 (or_1_out, not_1_out, not_2_out);
  and and_1 (UpDownMov, not_4_out, decoder_1_out2);
  and and_2 (and_2_out, decoder_1_out0, or_1_out);
  and and_3 (LeftRightMov, decoder_2_out1, not_2_out);
  Counter #(.max('hf), .width(4)) counter_1 (
    .clr(Reset), .up(UpDownMov), .count(not_3_out), .clk(FPS), .Q(Col_mov));  // open: load, D, carry
  Counter #(.max('hf), .width(4)) counter_2 (
    .clr(Reset), .up(LeftRightMov), .count(and_2_out), .clk(FPS), .Q(Row_mov));  // open: load, D, carry

  // Notes on the sheet:
  //   Set the Starting position to (2,e) //(row,col)
  //   Up/Down
  //   Right/Left
endmodule

module GrowBuzzer (
  input  Reset,
  input  Grow,
  input  Clock5
);

  wire comparator_1_eq, comparator_1_lt, counter_1_carry, or_1_out, or_2_out, or_3_out;
  wire [3:0] counter_1_q;
  wire [13:0] rom_1_data;

  or or_1 (or_1_out, comparator_1_lt, Grow);
  or or_2 (or_2_out, Grow, Clock5);
  or or_3 (or_3_out, Reset, comparator_1_eq);
  Counter #(.max('hf), .width(4)) counter_1 (
    .clr(or_3_out), .count(or_1_out), .clk(or_2_out), .carry(counter_1_carry), .Q(counter_1_q));  // open: load, up, D
  ROM #(.addrWidth(4), .dataWidth(14)) rom_1 (.addr(counter_1_q), .data(rom_1_data));
  // Buzzer #(.smooth_level(8), .smooth_width(8), .vol_width(8)) buzzer_1: pin names not known; wires that end beside it: rom_1_data, 8'h60, 1'b1
  Comparator #(.width(14)) comparator_1 (
    .a(14'h1), .b(rom_1_data), .eq(comparator_1_eq), .lt(comparator_1_lt));  // open: gt

  // Notes on the sheet:
  //   contents of rom_1 (hex, n*v repeats v):
  //   0 5*2bc 5*30c 2bc 2bc 30c 30c 1
endmodule

module GameWonBuzzer (
  input  Reset,
  input  GameWon,
  input  Clock5
);

  wire comparator_1_eq, comparator_1_lt, counter_1_carry, d_ff_1_q, or_1_out, or_2_out;
  wire [3:0] counter_1_q;
  wire [13:0] rom_1_data;

  D_Flip_Flop d_ff_1 (.D(GameWon), .clk(GameWon), .Q(d_ff_1_q), .reset(or_2_out));  // open: Qn, preset
  or or_1 (or_1_out, comparator_1_lt, d_ff_1_q);
  or or_2 (or_2_out, Reset, comparator_1_eq);
  Counter #(.max('hf), .width(4)) counter_1 (
    .clr(or_2_out), .count(or_1_out), .clk(Clock5), .carry(counter_1_carry), .Q(counter_1_q));  // open: load, up, D
  ROM #(.addrWidth(4), .dataWidth(14)) rom_1 (.addr(counter_1_q), .data(rom_1_data));
  Comparator #(.width(14)) comparator_1 (
    .a(14'h1), .b(rom_1_data), .eq(comparator_1_eq), .lt(comparator_1_lt));  // open: gt
  // Buzzer #(.smooth_level(8), .smooth_width(8), .vol_width(8)) buzzer_1: pin names not known; wires that end beside it: rom_1_data, 8'h60, 1'b1

  // Notes on the sheet:
  //   contents of rom_1 (hex, n*v repeats v):
  //   0 190 190 200 190 190 200 200 258 258 190 258 3e8 3e8 4e8 1
endmodule

module GameLostBuzzer (
  input  Reset,
  input  GameLost,
  input  Clock5
);

  wire comparator_1_eq, comparator_1_lt, counter_1_carry, d_ff_1_q, or_1_out, or_2_out;
  wire [3:0] counter_1_q;
  wire [13:0] rom_1_data;

  D_Flip_Flop d_ff_1 (.D(GameLost), .clk(GameLost), .Q(d_ff_1_q), .reset(or_2_out));  // open: Qn, preset
  or or_1 (or_1_out, comparator_1_lt, d_ff_1_q);
  or or_2 (or_2_out, Reset, comparator_1_eq);
  Counter #(.max('hf), .width(4)) counter_1 (
    .clr(or_2_out), .count(or_1_out), .clk(Clock5), .carry(counter_1_carry), .Q(counter_1_q));  // open: load, up, D
  ROM #(.addrWidth(4), .dataWidth(14)) rom_1 (.addr(counter_1_q), .data(rom_1_data));
  Comparator #(.width(14)) comparator_1 (
    .a(14'h1), .b(rom_1_data), .eq(comparator_1_eq), .lt(comparator_1_lt));  // open: gt
  // Buzzer #(.smooth_level(8), .smooth_width(8), .vol_width(8)) buzzer_1: pin names not known; wires that end beside it: rom_1_data, 8'h60, 1'b1

  // Notes on the sheet:
  //   contents of rom_1 (hex, n*v repeats v):
  //   0 200 400 600 800 500 800 200 200 700 700 150 100 1
endmodule

module ClockGenerator (
  input  Reset,
  input  MainClock,
  input  Play,
  output Clock7,
  output Clock6,
  output Clock5,
  output Clock4,
  output Clock3,
  output Clock2,
  output Clock1,
  output SoundClock
);

  wire comparator_1_eq, counter_2_carry, not_1_out, or_1_out, undriven, undriven_2;
  wire [5:0] counter_1_q;
  wire [7:0] counter_2_q, rom_1_data;
  wire [15:0] rom_2_data;

  Counter #(.max('h3f), .width(6)) counter_1 (
    .clr(or_1_out), .count(undriven), .clk(comparator_1_eq), .Q(counter_1_q));  // open: load, up, D, carry
  or or_1 (or_1_out, counter_2_carry, Reset);
  ROM #(.addrWidth(6)) rom_1 (.addr(counter_1_q), .data(rom_1_data));
  not not_1 (not_1_out, comparator_1_eq);
  Counter counter_2 (
    .clr(Reset), .load(comparator_1_eq), .up(undriven_2), .count(not_1_out), .clk(MainClock), .D(rom_1_data),
    .carry(counter_2_carry), .Q(counter_2_q));
  ROM #(.dataWidth(16)) rom_2 (.addr(counter_2_q), .data({rom_2_data[15:6], SoundClock, rom_2_data[4:0]}));
  Comparator #(.width(16)) comparator_1 (
    .a({16{1'b0}}), .b({rom_2_data[15:6], SoundClock, rom_2_data[4:0]}), .eq(comparator_1_eq));  // open: gt, lt
  and and_1 (Clock7, rom_2_data[7], Play);
  and and_2 (Clock6, rom_2_data[6], Play);
  and and_3 (Clock5, SoundClock, Play);
  and and_4 (Clock4, Play, rom_2_data[3]);
  and and_5 (Clock3, Play, rom_2_data[2]);
  and and_6 (Clock2, Play, rom_2_data[1]);
  and and_7 (Clock1, Play, rom_2_data[0]);

  // Notes on the sheet:
  //   contents of rom_1 (hex, n*v repeats v):
  //   0 4 28 4 28 4 28 4 28 4 28 4 28 4 28 4 28 4 28 4 28 4 28 4 28 4 28 4 28 4 28 4 28 2a ff
  //   Inputs
  //   contents of rom_2 (hex, n*v repeats v):
  //   81 d 0 0 6 10 6 10 6 10 6 10 6 10 6 10 6 10 6 10 6 10 6 10 6 10 6 10 6 10 6 10 6 10 6 10 4*0 20 0 40
  //   149*0 6 10 6 10 6 10 6 10 6 10 6 10 6 10 6 10 6 10 6 10 6 10 6 10 6 10 6 10 6 10 6 10 6 10 6 10 6 10
  //   6 10 6 10 6 10 6 10 6 10 6 10 6 10 6 10 6 10 6 10 6 10 6 10 6 10
endmodule

module RAMSystem (
  input  Reset,
  input  Clock1,
  input  Clock2,
  input  Clock3,
  input  Grow,
  input  [7:0] SnakeHead,
  output [7:0] Score,
  output [3:0] SelectedRow,
  output [15:0] SnakeBody
);

  wire comparator_1_gt;
  wire [3:0] counter_1_q;
  wire [7:0] adder_1_out, multiplexer_1_out, multiplexer_2_out, ram_1_dout, subtractor_2_out;
  wire [7:4] SnakeHead1;

  Counter counter_1 (.clr(Reset), .clk(Clock2), .Q({SelectedRow, counter_1_q}));  // open: load, up, count, D, carry
  Counter counter_2 (.clr(Reset), .clk(Grow), .Q(Score));  // open: load, up, count, D, carry
  // Probe on {SnakeHead1, SnakeHead[3:0]}
  Adder adder_1 (.a(Score), .b(8'h4), .out(adder_1_out));  // open: cin, cout
  // Probe on SelectedRow
  Multiplexer #(.width(8)) multiplexer_1 (
    .in0({SelectedRow, counter_1_q}), .in1({SnakeHead1, SnakeHead[3:0]}), .out(multiplexer_1_out),
    .sel(Clock1));
  Multiplexer #(.width(8)) multiplexer_2 (
    .in0(subtractor_2_out), .in1(adder_1_out), .out(multiplexer_2_out), .sel(Clock1));
  // Probe on multiplexer_1_out
  RAM #(.clearpin("true"), .enables("line")) ram_1 (
    .addr(multiplexer_1_out), .we(1'b1), .clk(Clock3), .din(multiplexer_2_out), .dout(ram_1_dout), .clr(Reset));
  // Probe on {SnakeHead1, SnakeHead[3:0]}
  Subtractor #(.width(4)) subtractor_1 (.a(SnakeHead[7:4]), .b(4'b0001), .out(SnakeHead1));  // open: bin, bout
  Comparator comparator_1 (.a(ram_1_dout), .b({8{1'b0}}), .gt(comparator_1_gt));  // open: eq, lt
  Subtractor subtractor_2 (.a(ram_1_dout), .b({8{1'b0}}), .out(subtractor_2_out), .bin(comparator_1_gt));  // open: bout
  // Shift_Register #(.length(16)) shift_register_1: pin names not known; wires that end beside it: Reset, Clock2, comparator_1_gt, SnakeBody[15], SnakeBody[14], SnakeBody[13], SnakeBody[12], SnakeBody[11], SnakeBody[10], SnakeBody[9], SnakeBody[8], SnakeBody[7], SnakeBody[6], SnakeBody[5], SnakeBody[4]
  // Probe on SnakeBody

  // Other names for the same wires on the sheet: SnakeHead1[3:0] = SnakeHead[3:0]

  // Notes on the sheet:
  //   Set the starting size for the snake body
endmodule

module FoodGenerator (
  input  Reset,
  input  Grow,
  input  Error,
  output [7:0] Food
);

  wire or_1_out;

  or or_1 (or_1_out, Grow, Error);
  Random random_1 (.clr(Reset), .clk(or_1_out), .out(Food));  // open: next

  // Notes on the sheet:
  //   Generate a Random location to the food
endmodule

module SoundSystem (
  input  Reset,
  input  SoundClock,
  input  SoundsON,
  input  Grow,
  input  GameWon,
  input  GameLost
);

  wire and_1_out, and_2_out, and_3_out;

  and and_1 (and_1_out, SoundsON, Grow);
  and and_2 (and_2_out, SoundsON, GameWon);
  and and_3 (and_3_out, SoundsON, GameLost);
  GrowBuzzer growbuzzer_1 (.Reset(Reset), .Grow(and_1_out), .Clock5(SoundClock));
  GameWonBuzzer gamewonbuzzer_1 (.Reset(Reset), .GameWon(and_2_out), .Clock5(SoundClock));
  GameLostBuzzer gamelostbuzzer_1 (.Reset(Reset), .GameLost(and_3_out), .Clock5(SoundClock));
endmodule

module DisplaySystem (
  input  Reset,
  input  Clock5,
  input  Clock6,
  input  [15:0] UpdatedRow,
  input  [3:0] SelectedRow,
  output [15:0] Out0,
  output [15:0] Out1,
  output [15:0] Out2,
  output [15:0] Out3,
  output [15:0] Out4,
  output [15:0] Out5,
  output [15:0] Out6,
  output [15:0] Out7,
  output [15:0] Out8,
  output [15:0] Out9,
  output [15:0] Out10,
  output [15:0] Out11,
  output [15:0] Out12,
  output [15:0] Out13,
  output [15:0] Out14,
  output [15:0] Out15
);

  wire [15:0] demultiplexer_1_out0, demultiplexer_1_out1, demultiplexer_1_out2, demultiplexer_1_out3,
       demultiplexer_1_out4, demultiplexer_1_out5, demultiplexer_1_out6, demultiplexer_1_out7,
       demultiplexer_1_out8, demultiplexer_1_out9, demultiplexer_1_out10, demultiplexer_1_out11,
       demultiplexer_1_out12, demultiplexer_1_out13, demultiplexer_1_out14, demultiplexer_1_out15,
       rowupdate_1_out0, rowupdate_1_out1, rowupdate_1_out2, rowupdate_1_out3, rowupdate_1_out4,
       rowupdate_1_out5, rowupdate_1_out6, rowupdate_1_out7, rowupdate_1_out8, rowupdate_1_out9,
       rowupdate_1_out10, rowupdate_1_out11, rowupdate_1_out12, rowupdate_1_out13, rowupdate_1_out14,
       rowupdate_1_out15;

  Demultiplexer #(.select(4), .width(16)) demultiplexer_1 (
    .out0(demultiplexer_1_out0), .out1(demultiplexer_1_out1), .out2(demultiplexer_1_out2),
    .out3(demultiplexer_1_out3), .out4(demultiplexer_1_out4), .out5(demultiplexer_1_out5),
    .out6(demultiplexer_1_out6), .out7(demultiplexer_1_out7), .out8(demultiplexer_1_out8),
    .out9(demultiplexer_1_out9), .out10(demultiplexer_1_out10), .out11(demultiplexer_1_out11),
    .out12(demultiplexer_1_out12), .out13(demultiplexer_1_out13), .out14(demultiplexer_1_out14),
    .out15(demultiplexer_1_out15), .in(UpdatedRow), .sel(SelectedRow));
  RowUpdate rowupdate_1 (
    .In0(demultiplexer_1_out0), .In1(demultiplexer_1_out1), .In2(demultiplexer_1_out2),
    .In3(demultiplexer_1_out3), .In4(demultiplexer_1_out4), .In5(demultiplexer_1_out5),
    .In6(demultiplexer_1_out6), .In7(demultiplexer_1_out7), .In8(demultiplexer_1_out8),
    .In9(demultiplexer_1_out9), .In10(demultiplexer_1_out10), .In11(demultiplexer_1_out11),
    .In12(demultiplexer_1_out12), .In13(demultiplexer_1_out13), .In14(demultiplexer_1_out14),
    .In15(demultiplexer_1_out15), .Reset(Reset), .Clock5(Clock5), .SelectedRow(SelectedRow),
    .Out0(rowupdate_1_out0), .Out1(rowupdate_1_out1), .Out2(rowupdate_1_out2), .Out3(rowupdate_1_out3),
    .Out4(rowupdate_1_out4), .Out5(rowupdate_1_out5), .Out6(rowupdate_1_out6), .Out7(rowupdate_1_out7),
    .Out8(rowupdate_1_out8), .Out9(rowupdate_1_out9), .Out10(rowupdate_1_out10), .Out11(rowupdate_1_out11),
    .Out12(rowupdate_1_out12), .Out13(rowupdate_1_out13), .Out14(rowupdate_1_out14), .Out15(rowupdate_1_out15));
  RowFinal rowfinal_1 (
    .In0(rowupdate_1_out0), .In1(rowupdate_1_out1), .In2(rowupdate_1_out2), .In3(rowupdate_1_out3),
    .In4(rowupdate_1_out4), .In5(rowupdate_1_out5), .In6(rowupdate_1_out6), .In7(rowupdate_1_out7),
    .In8(rowupdate_1_out8), .In9(rowupdate_1_out9), .In10(rowupdate_1_out10), .In11(rowupdate_1_out11),
    .In12(rowupdate_1_out12), .In13(rowupdate_1_out13), .In14(rowupdate_1_out14), .In15(rowupdate_1_out15),
    .Reset(Reset), .Clock6(Clock6), .Out0(Out0), .Out1(Out1), .Out2(Out2), .Out3(Out3), .Out4(Out4),
    .Out5(Out5), .Out6(Out6), .Out7(Out7), .Out8(Out8), .Out9(Out9), .Out10(Out10), .Out11(Out11),
    .Out12(Out12), .Out13(Out13), .Out14(Out14), .Out15(Out15));

  // Notes on the sheet:
  //   update the row
  //   Select Row from 0-15
  //   Save the updated row and keep the other rows unchanged
  //   Take all the rows data and display them
  //   Output
endmodule

module ManageSystem (
  input  Stop,
  input  PlayButton,
  input  SoundButton,
  input  WallButton,
  output Reset,
  output Play,
  output SoundsON,
  output WallMode
);

  wire d_ff_1_q, not_1_out;

  D_Flip_Flop d_ff_1 (.D(Stop), .clk(Stop), .Q(d_ff_1_q), .reset(not_1_out));  // open: Qn, preset
  not not_1 (not_1_out, Play);
  D_Flip_Flop d_ff_2 (.D(PlayButton), .clk(PlayButton), .Q(Play), .reset(d_ff_1_q));  // open: Qn, preset
  T_Flip_Flop t_ff_1 (.T(SoundButton), .clk(SoundButton), .Qn(SoundsON));  // open: Q, reset, preset
  T_Flip_Flop t_ff_2 (.T(WallButton), .clk(WallButton), .Q(WallMode));  // open: Qn, reset, preset

  assign Reset = PlayButton;

  // Notes on the sheet:
  //   Ensure that when buttonPlay pressed Play is ON 
  //   and when Stop pressed the Play is OFF and when clicked again it turn ON
  //   handle the Sound button // by deafults its ON 
  //   handle the Wall Mode button // by deafults its OFF
endmodule

module StopSystem (
  input  Reset,
  input  StopGame,
  input  GameWon,
  input  GameLost,
  input  Play,
  output Stop
);

  wire and_1_out, or_1_out;

  or or_1 (or_1_out, StopGame, GameWon, GameLost);
  and and_1 (and_1_out, or_1_out, Play);
  D_Flip_Flop d_ff_1 (.D(and_1_out), .clk(and_1_out), .Q(Stop), .reset(Reset));  // open: Qn, preset

  // Notes on the sheet:
  //   Input
  //   Handle when the Stop is turned ON
  //   Output
endmodule
